# Fritzing sketch snake_homeexam (saved by Fritzing 0.9.3b)
breadboards: 1

parts:
  Part2 = Arduino Uno (Rev3)
  J1 = female pin header, 13 pins [form="♀ (female)"]
  J2 = female pin header, 5 pins [form="♀ (female)"]
  SG1 = Buzzer 12mm [package=buzzer-12mm-ns]
  R1 = Resistor [tolerance=±5% resistance=220 package=THT]

nets:
  N1: Part2.A0, J2.pin3
  N2: Part2.A1, J2.pin2
  N3: Part2.A2, J2.pin1
  N4: Part2.D8, J1.pin6
  N5: Part2.D9_PWM, J1.pin5
  N6: Part2.D10_PWM/SS, J1.pin7
  N7: Part2.D11_PWM/MOSI, J1.pin4
  N8: Part2.D12/MISO, J1.pin9
  N9: Part2.D13/SCK, J1.pin3
  N10: Part2.D2, R1.Pin_0
  N11: Part2.D4, J1.pin8
  N12: Part2.5V, J1.pin1, J2.pin4
  N13: Part2.GND, J1.pin2, J2.pin5, SG1.2
  N14: SG1.1, R1.Pin_1

notes:
  This is the 1.8" tft-screen
  VCC, GND, !SCL, !SDA, DC, RES, CS, CS(microSD), MISO(microSD), X, Y, Z, Backlight
  This is the playstation joystick
  GND,
  +5V
  VRx,
  VRy,
  SW
